# Fritzing sketch Schemat (saved by Fritzing 0.9.3b)
breadboards: 1

parts:
  part = Resistor [tolerance=±5% resistance=100k package=THT]
  Q3 = LTR-301 [package=ltr-301]
  Q4 = LTR-301 [package=ltr-301]
  Q5 = NPN-Transistor [package="SOT-23 [SMD]"]
  Q6 = NPN-Transistor [package="TO92 [THT]"]
  part_2 = Resistor [tolerance=±5% resistance=50k package=THT]
  Q7 = Basic FET N-Channel [package="TO220 [THT]"]
  D1 = LTE-302 [package=lte-302]
  D2 = LTE-302 [package=lte-302]
  D3 = LTE-302 [package=lte-302]
  Nano = Arduino Nano (Rev3.0)
  Nano1 = Arduino Nano (Rev3.0)

nets:
  5V: part.Pin_0, part_2.Pin_0, D1.A
  N1: part.Pin_1, Q3.C, Q4.C
  N2: Q3.E, Q4.E, Q5.0
  N3: Q5.2, Q6.B
  N4: Q5.1, Q6.C, part_2.Pin_1, Nano1.A0
  GND: Q6.E, Q7.source
  N5: Q7.gate, Nano.D3
  N6: Q7.drain, D3.C
  N7: D1.C, D2.A
  N8: D2.C, D3.A
